# Fritzing sketch DC Motor Connection (saved by Fritzing 0.9.3b)

parts:
  Part3 = Arduino Uno (Rev3)  # not connected
  Part4 = Adafruit Motor/Stepper/Servo Shield [part_number="Adafruit #1438"]
  M2 = DC Motor
  VCC2 = 4 x AAA Battery Mount

nets:
  N1: Part4.M2A, M2.pin_1
  N2: Part4.M2B, M2.pin_2
  N3: Part4.GND, VCC2.-
  N4: Part4.VMOTOR, VCC2.+

custom parts:
  Adafruit Motor/Stepper/Servo Shield: The original Adafruit Motorshield kit is one of our most beloved kits, which is why we decided to make something even better. We have upgraded the shield kit to make the bestest, easiest way to drive DC and Stepper motors. This shield will make quick work of your next robotics project! We kept the ability to drive up to 4 DC motors or 2 stepper motors, but added many improvements: Instead of a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
